# Fritzing sketch UnoPermanente (saved by Fritzing 0.9.6b)
circuit board: 8.41712cm x 6.96256cm
breadboards: 1

parts:
  J1 = Screw terminal - 2 pins [package=THT]
  U1 = Voltage Regulator - 5V [package="TO220 [THT]"]
  C1 = Electrolytic Capacitor [capacitance=10µF voltage=35V package="100 mil [THT, electrolytic]"]
  IC1 = MICROCONTROLLER [package=dil28-3-zif_socket]
  S1 = Pushbutton [package="[THT]"]
  R1 = Resistor [tolerance=±5% power=0.25 resistance=10k package=THT]
  C3 = Ceramic Capacitor [capacitance=100nF voltage=35V package="100 mil [THT, multilayer]"]
  J2 = female pin header, 22 pins [form="♀ (female)"]

nets:
  N1: J1.pin1, C1.-
  N2: J1.pin2, U1.input_voltage, C1.+
  GND: U1.GND, IC1.GND, IC1.AGND, S1.Pin_1, S1.Pin_2, C3.1
  N3: U1.output_voltage, IC1.VCC, IC1.AVCC, IC1.AREF, R1.Pin_1, C3.0
  N4: IC1.PC6(_RESET), S1.Pin_3, S1.Pin_4, R1.Pin_0
  N5: IC1.PD0(RXD), J2.pin22
  N6: IC1.PD1(TXD), J2.pin21
  N7: IC1.PD2(INT0), J2.pin20
  N8: IC1.PD3(INT1), J2.pin19
  N9: IC1.PD4(XCK_T0), J2.pin18
  N10: IC1.PB6(XTAL1_TOSC1), J2.pin17
  N11: IC1.PB7(XTAL2_TOSC2), J2.pin16
  N12: IC1.PD5(T1), J2.pin15
  N13: IC1.PD6(AIN0), J2.pin14
  N14: IC1.PD7(AIN1), J2.pin13
  N15: IC1.PB0(ICP), J2.pin12
